// Logisim project counter.circ as structural Verilog: 3 circuits, main circuit main
module main (
  input  in_1,
  output D0,
  output D1,
  output D2,
  output D3
);

  wire and_1_out, not_1_out, or_1_out, por_1_out, t_1_q;

  POR por_1 (.out(por_1_out));
  or or_1 (or_1_out, and_1_out, por_1_out);
  T t_1 (.C(in_1), .POR(or_1_out), .Q(t_1_q));  // open: NQ
  T t_2 (.C(t_1_q), .POR(por_1_out), .Q(D1));  // open: NQ
  T t_3 (.C(D1), .POR(por_1_out), .Q(D2));  // open: NQ
  T t_4 (.C(D2), .POR(por_1_out), .Q(D3));  // open: NQ
  and and_1 (and_1_out, D3, D2, D1);
  not not_1 (not_1_out, and_1_out);
  and and_2 (D0, not_1_out, t_1_q);
  Hex_Digit_Display hex_digit_display_1 (.value({D3, D2, D1, D0}));  // open: dp
endmodule

module T (
  input  C,
  input  POR,
  output Q,
  output NQ
);

  wire dff_1_q, not_1_out, not_2_out;

  not not_1 (not_1_out, C);
  not not_2 (not_2_out, Q);
  Dff dff_1 (.C(not_1_out), .D(not_2_out), .Q(dff_1_q));  // open: POR, NQ
  Dff dff_2 (.C(C), .POR(POR), .D(dff_1_q), .NQ(NQ), .Q(Q));

  // Notes on the sheet:
  //   2
  //   1
endmodule

module Dff (
  input  D,
  input  C,
  input  POR,
  output Q,
  output NQ
);

  wire nand_1_out, nand_2_out, nand_4_out, not_1_out;

  nand nand_1 (nand_1_out, D, C);
  not not_1 (not_1_out, D);
  nand nand_2 (nand_2_out, not_1_out, C);
  nand nand_3 (Q, nand_1_out, NQ);
  nand nand_4 (nand_4_out, Q, nand_2_out);
  or or_1 (NQ, nand_4_out, POR);
endmodule
