// Logisim project lfsr.circ as structural Verilog: 3 circuits, main circuit main
module main (
  input  C,
  input  POR,
  output R
);

  wire xor_1_out;
  wire [0:0] mc_1_q;
  wire [3:1] mc_4_q;

  MC mc_1 (.IV(1'b0), .POR(POR), .D(R), .C(C), .Q(mc_1_q[0]));
  MC mc_2 (.IV(1'b0), .POR(POR), .D(mc_1_q[0]), .C(C), .Q(mc_4_q[3]));
  xor xor_1 (xor_1_out, R, mc_4_q[3]);
  MC mc_3 (.IV(1'b0), .POR(POR), .D(xor_1_out), .C(C), .Q(mc_4_q[2]));
  MC mc_4 (.IV(1'b0), .POR(POR), .D(mc_4_q[2]), .C(C), .Q(mc_4_q[1]));
  Hex_Digit_Display hex_digit_display_1 (.value({3'b000, mc_1_q[0]}));  // open: dp
  MC mc_5 (.IV(1'b1), .POR(POR), .D(mc_4_q[1]), .C(C), .Q(R));
  Hex_Digit_Display hex_digit_display_2 (.value({mc_4_q, R}));  // open: dp
endmodule

module Dff (
  input  S1,
  input  D,
  input  C,
  input  S0,
  output Q,
  output NQ
);

  wire nand_1_out, nand_2_out, nand_3_out, nand_4_out, not_1_out;

  not not_1 (not_1_out, D);
  nand nand_1 (nand_1_out, D, C);
  nand nand_2 (nand_2_out, not_1_out, C);
  nand nand_3 (nand_3_out, nand_1_out, NQ);
  nand nand_4 (nand_4_out, Q, nand_2_out);
  or or_1 (Q, S1, nand_3_out);
  or or_2 (NQ, nand_4_out, S0);
endmodule

module MC (
  input  D,
  input  C,
  input  IV,
  input  POR,
  output Q
);

  wire and_1_out, and_2_out, dff_1_q, not_1_out, not_2_out;

  not not_1 (not_1_out, IV);
  and and_1 (and_1_out, IV, POR);
  and and_2 (and_2_out, not_1_out, POR);
  Dff dff_1 (.S1(and_1_out), .S0(and_2_out), .D(D), .C(C), .Q(dff_1_q));  // open: NQ
  not not_2 (not_2_out, C);
  Dff dff_2 (.S1(and_1_out), .S0(and_2_out), .D(dff_1_q), .C(not_2_out), .Q(Q));  // open: NQ
endmodule
